// Logisim project hrmcpu.circ as structural Verilog: 10 circuits, main circuit TOP
module TOP (
  input  in_1
);

  wire alu_1_flag, branch, clock_1_out, empty, full, ijump, nxtINSTR, rIN, rst, rstPC, srcA, undriven, wAR,
       wIR, wM, wO, wPC, wR;
  wire [1:0] muxR;
  wire [2:0] aluCtl;
  wire [7:0] alu_1_aluout, inbox_1_din, INSTR, memory_1_m, pc_1_pc, prog_1_data, r_1_r;

  // Probe on prog_1_data
  PROG prog_1 (.Addr(pc_1_pc), .Data(prog_1_data));
  // Probe on INSTR
  IR ir_1 (.nIR(prog_1_data), .wIR(wIR), .rIR(INSTR));
  // Probe on inbox_1_din
  INBOX inbox_1 (.rIn(rIN), .rst(rst), .empty(empty), .DIN(inbox_1_din));
  LED lEmpty (.in(empty));
  // Probe on r_1_r
  R r_1 (.iInbox(inbox_1_din), .iMem(memory_1_m), .iAlu(alu_1_aluout), .muxR(muxR), .wR(wR), .R(r_1_r));
  // Probe on memory_1_m
  MEMORY memory_1 (.ADDR(prog_1_data), .srcA(srcA), .wM(wM), .R(r_1_r), .wAR(wAR), .M(memory_1_m));
  PC pc_1 (
    .branch(branch), .ijump(ijump), .aluFlag(alu_1_flag), .jmpAddr(prog_1_data), .wPC(wPC), .rst(rstPC),
    .PC(pc_1_pc));
  ALU alu_1 (.inR(r_1_r), .inM(memory_1_m), .aluCtl(aluCtl), .flag(alu_1_flag), .aluOut(alu_1_aluout));
  // Probe on alu_1_aluout
  // Probe on pc_1_pc
  OUTBOX outbox_1 (.DOUT(r_1_r), .wO(wO), .full(full));
  Clock clock_1 (.out(clock_1_out));
  // FSM_Entity #(.content("fsm ControlUnit @[ 34 , 30 , 1400 , 900 ]\n{ in INSTR [ 8 ] @[ 34 , 100 , 71 , 15 ]\n;\nin inEmpty [ 1 ] @[ 34 , 132 , 55 , 15 ]\n;\nin outFull [ 1 ] @[ 34 , 167 , 48 , 15 ]\n;\nin debug [ 1 ] @[ 34 , 204 , 46 , 15 ]\n;\nin nxtInstr [ 1 ] @[ 34 , 240 , 53 , 15 ]\n;\nout wIR [ 1 ] @[ 1408 , 93 , 26 , 15 ]\n;\nout muxR [ 2 ] @[ 1365 , 150 , 69 , 15 ]\n;\nout wR [ 1 ] @[ 1411 , 177 , 23 , 15 ]\n;\nout srcA [ 1 ] @[ 1401 , 244 , 33 , 15 ]\n;\nout wM [ 1 ] @[ 1409 , 268 , 25 , 15 ]\n;\nout wAR [ 1 ] @[ 1403 , 303 , 31 , 15 ]\n;\nout aluCtl [ 3 ] @[ 1363 , 333 , 71 , 15 ]\n;\nout wPC [ 1 ] @[ 1403 , 366 , 31 , 15 ]\n;\nout rIn [ 1 ] @[ 1412 , 390 , 22 , 15 ]\n;\nout wO [ 1 ] @[ 1410 , 415 , 24 , 15 ]\n;\nout ijump [ 1 ] @[ 1395 , 467 , 39 , 15 ]\n;\nout branch [ 1 ] @[ 1384 , 490 , 50 , 15 ]\n;\nout rst [ 1 ] @[ 1411 , 523 , 23 , 15 ]\n;\nout halt [ 1 ] @[ 1404 , 553 , 30 , 15 ]\n;\ncodeWidth = 6 ; reset = RESET ; state RESET = \"000000\" @[ 105 , 72 , 30 , 30 ]\n{\ncommands @[ 114 , 123 , 53 , 21 ]\n{\nrst = \"1\" ;\n}\ntransitions {\nRESET -> FETCH_I when default @[ 271 , 70 , 50 , 21 ]\n;\n}\n}\nstate Inc_PC = \"000010\" @[ 56 , 272 , 30 , 30 ]\n{\ncommands @[ 53 , 324 , 61 , 21 ]\n{\nwPC = \"1\" ;\n}\ntransitions {\nInc_PC -> FETCH_I when default @[ 152 , 161 , 50 , 21 ]\n;\n}\n}\nstate FETCH_I = \"000100\" @[ 451 , 71 , 30 , 30 ]\n{\ncommands @[ 499 , 117 , 56 , 21 ]\n{\nwIR = \"0\" ;\n}\ntransitions {\nFETCH_I -> LOAD_IR when default @[ 463 , 149 , 50 , 21 ]\n;\nFETCH_I -> WAIT_KEY when debug == \"1\" @[ 268 , 153 , 94 , 21 ]\n;\n}\n}\nstate INBOX1 = \"000110\" @[ 332 , 637 , 30 , 30 ]\n{\ncommands @[ 377 , 652 , 52 , 21 ]\n{\nrIn = \"1\" ;\n}\ntransitions {\nINBOX1 -> INBOX2 when default @[ 291 , 690 , 50 , 21 ]\n;\n}\n}\nstate INBOX2 = \"001000\" @[ 235 , 725 , 30 , 30 ]\n{\ncommands @[ 280 , 740 , 77 , 36 ]\n{\nmuxR = \"00\" ;\nwR = \"1\" ;\n}\ntransitions {\nINBOX2 -> Inc_PC when default @[ 58 , 619 , 50 , 21 ]\n;\n}\n}\nstate OUTBOX = \"001010\" @[ 153 , 555 , 30 , 30 ]\n{\ncommands @[ 198 , 570 , 54 , 21 ]\n{\nwO = \"1\" ;\n}\ntransitions {\nOUTBOX -> Inc_PC when default @[ 44 , 514 , 50 , 21 ]\n;\n}\n}\nstate INCPC2 = \"001100\" @[ 652 , 157 , 30 , 30 ]\n{\ncommands @[ 715 , 170 , 61 , 21 ]\n{\nwPC = \"1\" ;\n}\ntransitions {\nINCPC2 -> FETCH_O when default @[ 662 , 225 , 50 , 21 ]\n;\n}\n}\nstate READMEM = \"001110\" @[ 686 , 503 , 30 , 30 ]\n{\ncommands @[ 731 , 518 , 63 , 21 ]\n{\nsrcA = \"0\" ;\n}\ntransitions {\nREADMEM -> BUMPP when INSTR [ 7 : 4 ] == \"0110\" @[ 739 , 651 , 143 , 21 ]\n;\nREADMEM -> BUMPN when INSTR [ 7 : 4 ] == \"0111\" @[ 804 , 618 , 143 , 21 ]\n;\nREADMEM -> COPYFROM when INSTR [ 7 : 4 ] == \"0010\" @[ 533 , 641 , 143 , 21 ]\n;\nREADMEM -> ADD when INSTR [ 7 : 4 ] == \"0100\" @[ 604 , 676 , 143 , 21 ]\n;\nREADMEM -> HALT when default @[ 578 , 494 , 50 , 21 ]\n;\nREADMEM -> SUB when INSTR [ 7 : 4 ] == \"0101\" @[ 644 , 702 , 143 , 21 ]\n;\n}\n}\nstate COPYFROM = \"010000\" @[ 495 , 727 , 30 , 30 ]\n{\ncommands @[ 540 , 742 , 77 , 36 ]\n{\nmuxR = \"01\" ;\nwR = \"1\" ;\n}\ntransitions {\nCOPYFROM -> Inc_PC when default @[ 90 , 722 , 50 , 21 ]\n;\n}\n}\nstate DECODE = \"010010\" @[ 348 , 284 , 30 , 30 ]\n{\ncommands @[ 393 , 299 , 30 , 20 ]\n{\n}\ntransitions {\nDECODE -> OUTBOX when INSTR [ 7 : 4 ] == \"0001\" . outFull == \"0\" @[ 173 , 423 ,\n247 , 21 ]\n;\nDECODE -> INBOX1 when INSTR [ 7 : 4 ] == \"0000\" . inEmpty == \"0\" @[ 237 , 462 ,\n254 , 21 ]\n;\nDECODE -> HALT when INSTR [ 7 : 4 ] == \"1111\" @[ 371 , 486 , 143 , 21 ]\n;\nDECODE -> INCPC2 when default @[ 496 , 233 , 50 , 21 ]\n;\nDECODE -> WAIT_INBOX when INSTR [ 7 : 4 ] == \"0000\" . inEmpty == \"1\" @[ 397 ,\n356 , 254 , 21 ]\n;\nDECODE -> WAIT_OUTBOX when INSTR [ 7 : 4 ] == \"0001\" . outFull == \"1\" @[ 124 ,\n320 , 247 , 21 ]\n;\n}\n}\nstate HALT = \"010100\" @[ 463 , 569 , 30 , 30 ]\n{\ncommands @[ 468 , 618 , 60 , 21 ]\n{\nhalt = \"1\" ;\n}\n}\nstate COPYTO = \"010110\" @[ 1303 , 851 , 30 , 30 ]\n{\ncommands @[ 1347 , 866 , 55 , 21 ]\n{\nwM = \"1\" ;\n}\ntransitions {\nCOPYTO -> Inc_PC when default @[ 74 , 794 , 50 , 21 ]\n;\n}\n}\nstate JUMP = \"011000\" @[ 818 , 138 , 30 , 30 ]\n{\ncommands @[ 847 , 186 , 80 , 51 ]\n{\nbranch = \"1\" ;\nijump = \"1\" ;\nwPC = \"1\" ;\n}\ntransitions {\nJUMP -> FETCH_I when default @[ 679 , 111 , 50 , 21 ]\n;\n}\n}\nstate LOAD_IR = \"011010\" @[ 410 , 173 , 30 , 30 ]\n{\ncommands @[ 428 , 222 , 56 , 21 ]\n{\nwIR = \"1\" ;\n}\ntransitions {\nLOAD_IR -> DECODE when default @[ 387 , 246 , 50 , 21 ]\n;\n}\n}\nstate FETCH_O = \"011100\" @[ 654 , 258 , 30 , 30 ]\n{\ncommands @[ 625 , 284 , 30 , 20 ]\n{\n}\ntransitions {\nFETCH_O -> JUMP when INSTR [ 7 : 4 ] == \"1000\" @[ 735 , 239 , 143 , 21 ]\n;\nFETCH_O -> JUMPZ when INSTR [ 7 : 4 ] == \"1001\" @[ 803 , 265 , 143 , 21 ]\n;\nFETCH_O -> JUMPN when INSTR [ 7 : 4 ] == \"1010\" @[ 902 , 289 , 143 , 21 ]\n;\nFETCH_O -> LOAD_AR when default @[ 704 , 315 , 50 , 21 ]\n;\n}\n}\nstate ADD = \"011110\" @[ 595 , 781 , 30 , 30 ]\n{\ncommands @[ 592 , 831 , 87 , 51 ]\n{\nmuxR = \"11\" ;\naluCtl = \"000\" ;\nwR = \"1\" ;\n}\ntransitions {\nADD -> Inc_PC when default @[ 96 , 768 , 50 , 21 ]\n;\n}\n}\nstate SUB = \"100000\" @[ 719 , 784 , 30 , 30 ]\n{\ncommands @[ 715 , 834 , 87 , 51 ]\n{\nmuxR = \"11\" ;\naluCtl = \"001\" ;\nwR = \"1\" ;\n}\ntransitions {\nSUB -> Inc_PC when default @[ 60 , 821 , 50 , 21 ]\n;\n}\n}\nstate WAIT_INBOX = \"100010\" @[ 484 , 388 , 30 , 30 ]\n{\ncommands @[ 506 , 437 , 30 , 20 ]\n{\n}\ntransitions {\nWAIT_INBOX -> INBOX1 when inEmpty == \"0\" @[ 384 , 518 , 103 , 21 ]\n;\n}\n}\nstate JUMPZ = \"100100\" @[ 932 , 134 , 30 , 30 ]\n{\ncommands @[ 956 , 184 , 87 , 66 ]\n{\nbranch = \"1\" ;\nijump = \"0\" ;\naluCtl = \"000\" ;\nwPC = \"1\" ;\n}\ntransitions {\nJUMPZ -> FETCH_I when default @[ 736 , 88 , 50 , 21 ]\n;\n}\n}\nstate JUMPN = \"100110\" @[ 1043 , 136 , 30 , 30 ]\n{\ncommands @[ 1069 , 185 , 87 , 66 ]\n{\nbranch = \"1\" ;\nijump = \"0\" ;\naluCtl = \"100\" ;\nwPC = \"1\" ;\n}\ntransitions {\nJUMPN -> FETCH_I when default @[ 801 , 69 , 50 , 21 ]\n;\n}\n}\nstate BUMPP = \"101000\" @[ 830 , 732 , 30 , 30 ]\n{\ncommands @[ 836 , 781 , 87 , 51 ]\n{\nmuxR = \"11\" ;\naluCtl = \"010\" ;\nwR = \"1\" ;\n}\ntransitions {\nBUMPP -> COPYTO when default @[ 1040 , 810 , 50 , 21 ]\n;\n}\n}\nstate BUMPN = \"101010\" @[ 922 , 664 , 30 , 30 ]\n{\ncommands @[ 923 , 712 , 87 , 51 ]\n{\nmuxR = \"11\" ;\naluCtl = \"011\" ;\nwR = \"1\" ;\n}\ntransitions {\nBUMPN -> COPYTO when default @[ 1177 , 776 , 50 , 21 ]\n;\n}\n}\nstate WAIT_OUTBOX = \"101100\" @[ 159 , 351 , 30 , 30 ]\n{\ncommands @[ 199 , 397 , 30 , 20 ]\n{\n}\ntransitions {\nWAIT_OUTBOX -> OUTBOX when outFull == \"0\" @[ 140 , 473 , 96 , 21 ]\n;\n}\n}\nstate LOAD_AR = \"101110\" @[ 657 , 332 , 30 , 30 ]\n{\ncommands @[ 659 , 382 , 61 , 21 ]\n{\nwAR = \"1\" ;\n}\ntransitions {\nLOAD_AR -> COPYTO when INSTR [ 7 : 4 ] == \"0011\" . INSTR [ 3 : 3 ] == \"0\" @[\n1115 , 383 , 270 , 21 ]\n;\nLOAD_AR -> READMEM2 when INSTR [ 3 : 3 ] == \"1\" @[ 727 , 391 , 119 , 21 ]\n;\nLOAD_AR -> READMEM when default @[ 652 , 433 , 50 , 21 ]\n;\n}\n}\nstate LOAD_AR2 = \"110000\" @[ 885 , 454 , 30 , 30 ]\n{\ncommands @[ 884 , 505 , 63 , 36 ]\n{\nsrcA = \"1\" ;\nwAR = \"1\" ;\n}\ntransitions {\nLOAD_AR2 -> READMEM when default @[ 780 , 476 , 50 , 21 ]\n;\nLOAD_AR2 -> COPYTO when INSTR [ 7 : 4 ] == \"0011\" @[ 1109 , 621 , 143 , 21 ]\n;\n}\n}\nstate READMEM2 = \"110010\" @[ 880 , 352 , 30 , 30 ]\n{\ncommands @[ 891 , 404 , 30 , 20 ]\n{\n}\ntransitions {\nREADMEM2 -> LOAD_AR2 when default @[ 935 , 428 , 50 , 21 ]\n;\n}\n}\nstate WAIT_KEY = \"110100\" @[ 205 , 188 , 30 , 30 ]\n{\ncommands @[ 219 , 237 , 30 , 20 ]\n{\n}\ntransitions {\nWAIT_KEY -> LOAD_IR when nxtInstr == \"1\" @[ 274 , 250 , 101 , 21 ]\n;\n}\n}\n}")) ControlUnit: pin names not known; wires that end beside it: clock_1_out, rst, 1'b1, INSTR, empty, full, in_1, nxtINSTR, wIR, muxR, wR, srcA, wM, wAR, aluCtl, wPC, rIN, wO, ijump, branch
  Button rstBtn (.out(rst));
  Button button_1 (.out(nxtINSTR));
  LED Halt (.in(undriven));

  // Other names for the same wires on the sheet: debug = in_1

  // Notes on the sheet:
  //   HRM CPU
  //   @adumont
endmodule

module PC (
  input  branch,
  input  ijump,
  input  aluFlag,
  input  [7:0] jmpAddr,
  input  wPC,
  input  rst,
  output [7:0] PC
);

  wire and_1_out, clock_1_out, or_1_out, or_2_out;
  wire [7:0] adder_1_out, multiplexer_1_out, multiplexer_2_out;

  or or_1 (or_1_out, ijump, aluFlag);
  and and_1 (and_1_out, branch, or_1_out);
  Multiplexer #(.width(8), .enable("false")) multiplexer_1 (
    .in0(adder_1_out), .in1(jmpAddr), .out(multiplexer_1_out), .sel(and_1_out));
  Multiplexer #(.width(8), .enable("false")) multiplexer_2 (
    .in0(multiplexer_1_out), .in1({8{1'b0}}), .out(multiplexer_2_out), .sel(rst));
  // Probe on multiplexer_2_out
  or or_2 (or_2_out, rst, wPC);
  Register rPC (.D(multiplexer_2_out), .en(or_2_out), .clk(clock_1_out), .Q(PC));  // open: clr
  Clock clock_1 (.out(clock_1_out));
  // Probe on adder_1_out
  Adder adder_1 (.a(PC), .b(8'h1), .out(adder_1_out));  // open: cin, cout
endmodule

module INBOX (
  input  rIn,
  input  rst,
  output empty,
  output [7:0] DIN
);

  wire clock_1_out, clock_3_out, fsm_entity_1_p1, or_1_out, s1, s2;
  wire [7:0] adder_1_out, adder_2_out, inCursor_q, register_1_q, undriven;

  Clock clock_1 (.out(clock_1_out));
  // FSM_Entity #(.content("fsm InboxInit @[ 50 , 50 , 800 , 500 ]\n{ out s1 [ 1 ] @[ 829 , 99 , 21 , 15 ]\n;\nout s2 [ 1 ] @[ 829 , 137 , 21 , 15 ]\n;\ncodeWidth = 3 ; reset = S0 ; state S0 = \"000\" @[ 80 , 101 , 30 , 30 ]\n{\ncommands @[ 123 , 115 , 51 , 21 ]\n{\ns1 = \"0\" ;\n}\ntransitions {\nS0 -> S1 when default @[ 257 , 115 , 50 , 21 ]\n;\n}\n}\nstate S1 = \"010\" @[ 407 , 107 , 30 , 30 ]\n{\ncommands @[ 452 , 122 , 51 , 21 ]\n{\ns1 = \"1\" ;\n}\ntransitions {\nS1 -> S2 when default @[ 337 , 199 , 50 , 21 ]\n;\n}\n}\nstate S2 = \"100\" @[ 313 , 247 , 30 , 30 ]\n{\ncommands @[ 358 , 262 , 51 , 21 ]\n{\ns2 = \"1\" ;\n}\ntransitions {\nS2 -> S4 when default @[ 444 , 248 , 50 , 21 ]\n;\n}\n}\nstate S4 = \"001\" @[ 526 , 263 , 30 , 30 ]\n{\ncommands @[ 571 , 278 , 30 , 20 ]\n{\n}\n}\n}")) fsm_entity_1: pin names not known; wires that end beside it: fsm_entity_1_p1, rst, 1'b1, s1, s2
  Clock clock_2 (.out(fsm_entity_1_p1));
  or or_1 (or_1_out, rIn, s2);
  Register inCursor (.D(adder_1_out), .en(or_1_out), .clk(clock_1_out), .Q(inCursor_q), .clr(rst));
  ROM rom_1 (.addr(inCursor_q));  // open: data
  Adder adder_1 (.a(inCursor_q), .b(8'h1), .out(adder_1_out));  // open: cin, cout
  Register register_1 (.D(DIN), .en(s1), .clk(clock_1_out), .Q(register_1_q), .clr(rst));
  Adder adder_2 (.a(register_1_q), .b(8'h1), .out(adder_2_out));  // open: cin, cout
  Clock clock_3 (.out(clock_3_out));
  Register inboxData (.D(undriven), .en(1'b1), .clk(clock_3_out), .Q(DIN), .clr(rst));
  Comparator comparator_1 (.a(inCursor_q), .b(adder_2_out), .eq(empty));  // open: gt, lt

  // Notes on the sheet:
  //   contents of rom_1 (hex, n*v repeats v):
  //   4 1 2 3 4
endmodule

module IR (
  input  [7:0] nIR,
  input  wIR,
  output [7:0] rIR
);

  wire clock_1_out;

  Register IR (.D(nIR), .en(wIR), .clk(clock_1_out), .Q(rIR));  // open: clr
  Clock clock_1 (.out(clock_1_out));
endmodule

module R (
  input  [7:0] iInbox,
  input  [7:0] iMem,
  input  [7:0] iAlu,
  input  [1:0] muxR,
  input  wR,
  output [7:0] R
);

  wire clock_1_out;
  wire [7:0] multiplexer_1_out;

  Multiplexer #(.select(2), .width(8), .enable("false")) multiplexer_1 (
    .in0(iInbox), .in1(iMem), .in3(iAlu), .out(multiplexer_1_out), .sel(muxR));  // open: in2
  Register register_1 (.D(multiplexer_1_out), .en(wR), .clk(clock_1_out), .Q(R));  // open: clr
  Clock clock_1 (.out(clock_1_out));
endmodule

module OUTBOX (
  input  [7:0] DOUT,
  input  wO,
  output full
);

  wire clock_1_out, clock_2_out;
  wire [5:0] adder_1_out, register_1_q;

  Clock clock_1 (.out(clock_1_out));
  Register #(.width(6)) register_1 (.D(adder_1_out), .en(wO), .clk(clock_1_out), .Q(register_1_q));  // open: clr
  Adder #(.width(6)) adder_1 (.a(register_1_q), .b(6'b000001), .out(adder_1_out));  // open: cin, cout
  // RAM #(.addrWidth(6)) ram_1: pin names not known; wires that end beside it: register_1_q, DOUT
  Clock clock_2 (.out(clock_2_out));
  Comparator #(.width(6), .mode("unsigned")) comparator_1 (.a(register_1_q), .b({6{1'b1}}), .eq(full));  // open: gt, lt
endmodule

module MEMORY (
  input  [7:0] ADDR,
  input  srcA,
  input  wM,
  input  [7:0] R,
  input  wAR,
  output [7:0] M
);

  wire clock_1_out, clock_2_out;
  wire [7:0] AR_q, multiplexer_1_out;

  Multiplexer #(.width(8), .enable("false")) multiplexer_1 (.in0(ADDR), .in1(M), .out(multiplexer_1_out), .sel(srcA));
  // Probe on multiplexer_1_out
  Register AR (.D(multiplexer_1_out), .en(wAR), .clk(clock_1_out), .Q(AR_q));  // open: clr
  Clock clock_1 (.out(clock_1_out));
  // Probe on AR_q
  Clock clock_2 (.out(clock_2_out));
  RAM #(.databus("bibus")) ram_1 (.clk(AR_q[0]));  // open: addr, we, din, dout
  // Probe on R
  // Pins of 1 and 8 bits meet at AR_q

  // Notes on the sheet:
  //   contents of ram_1 (hex, n*v repeats v):
  //   2 1 4 2 3 4 1 2 1 4 3 2 1 2 7*0 1 3 0 0 a
endmodule

module ALU (
  input  [7:0] inR,
  input  [7:0] inM,
  input  [2:0] aluCtl,
  output flag,
  output [7:0] aluOut
);

  wire comparator_1_eq, comparator_1_lt;
  wire [7:0] adder_1_out, adder_2_out, multiplexer_2_out, multiplexer_3_out, subtractor_1_out,
       subtractor_2_out;

  // Probe on inR
  // Probe on inM
  Comparator comparator_1 (.a(inR), .b({8{1'b0}}), .eq(comparator_1_eq), .lt(comparator_1_lt));  // open: gt
  Adder adder_1 (.a(inR), .b(inM), .out(adder_1_out));  // open: cin, cout
  Subtractor subtractor_1 (.a(inR), .b(inM), .out(subtractor_1_out));  // open: bin, bout
  Adder adder_2 (.a(inM), .b(8'h1), .out(adder_2_out));  // open: cin, cout
  Subtractor subtractor_2 (.a(inM), .b(8'h1), .out(subtractor_2_out));  // open: bin, bout
  Multiplexer #(.enable("false")) multiplexer_1 (
    .in0(comparator_1_eq), .in1(comparator_1_lt), .out(flag), .sel(aluCtl[2]));
  Multiplexer #(.width(8), .enable("false")) multiplexer_2 (
    .in0(adder_1_out), .in1(subtractor_1_out), .out(multiplexer_2_out), .sel(aluCtl[0]));
  Multiplexer #(.width(8), .enable("false")) multiplexer_3 (
    .in0(adder_2_out), .in1(subtractor_2_out), .out(multiplexer_3_out), .sel(aluCtl[0]));
  Multiplexer #(.width(8), .enable("false")) multiplexer_4 (
    .in0(multiplexer_2_out), .in1(multiplexer_3_out), .out(aluOut), .sel(aluCtl[1]));
endmodule

module tmp (
  input  in_1,
  input  in_2,
  input  [1:0] muxR,
  input  in_4,
  input  in_5,
  input  in_6,
  input  in_7,
  input  in_8,
  input  ijump,
  input  [2:0] aluCtl,
  input  in_11,
  input  in_12,
  input  wPC,
  input  [2:0] in_14,
  input  wO,
  output [3:0] out_16
);

  wire clock_1_out;

  Clock clock_1 (.out(clock_1_out));
  // FSM_Entity #(.content("fsm example @[ 50 , 50 , 800 , 500 ]\n{ in A [ 3 ] @[ 50 , 100 , 44 , 15 ]\n;\nout X [ 4 ] @[ 807 , 140 , 43 , 15 ]\n;\ncodeWidth = 2 ; reset = S0 ; state S0 = \"00\" @[ 249 , 171 , 30 , 30 ]\n{\ncommands @[ 294 , 186 , 67 , 21 ]\n{\nX = \"0001\" ;\n}\ntransitions {\nS0 -> S1 when default @[ 372 , 148 , 50 , 21 ]\n;\nS0 -> S3 when A == \"000\" @[ 346 , 269 , 78 , 21 ]\n;\n}\n}\nstate S1 = \"10\" @[ 467 , 146 , 30 , 30 ]\n{\ncommands @[ 512 , 161 , 67 , 21 ]\n{\nX = \"0010\" ;\n}\ntransitions {\nS1 -> S2 when default @[ 533 , 276 , 50 , 21 ]\n;\nS1 -> S0 when A == \"000\" @[ 376 , 216 , 78 , 21 ]\n;\n}\n}\nstate S2 = \"00\" @[ 471 , 339 , 30 , 30 ]\n{\ncommands @[ 543 , 353 , 131 , 21 ]\n{\nX = { \"00\" , A [ 1 : 0 ] , \"1\" } ;\n}\ntransitions {\nS2 -> S3 when default @[ 392 , 398 , 50 , 21 ]\n;\nS2 -> S1 when A [ 2 : 1 ] == \"11\" @[ 557 , 250 , 100 , 21 ]\n;\n}\n}\nstate S3 = \"10\" @[ 265 , 329 , 30 , 30 ]\n{\ncommands @[ 310 , 344 , 67 , 21 ]\n{\nX = \"1000\" ;\n}\ntransitions {\nS3 -> S0 when default @[ 248 , 278 , 50 , 21 ]\n;\nS3 -> S2 when A == \"000\" @[ 388 , 313 , 78 , 21 ]\n;\n}\n}\n}")) fsm_entity_1: pin names not known; wires that end beside it: clock_1_out, in_11, in_12, in_14, out_16

  // Other names for the same wires on the sheet: branch = in_8; muxM = in_4; rIN = in_2; srcA = in_5; wIR = in_1;
  //   wM = in_7; wR = in_6
endmodule

module PROG (
  input  [7:0] Addr,
  output [7:0] Data
);

  wire clock_1_out;
  wire [7:0] undriven;

  ROM rom_1 (.addr(Addr));  // open: data
  Register register_1 (.D(undriven), .en(1'b1), .clk(clock_1_out), .Q(Data), .clr(1'b0));
  Clock clock_1 (.out(clock_1_out));

  // Notes on the sheet:
  //   contents of rom_1 (hex, n*v repeats v):
  //   20 14 30 19 30 16 0 30 15 28 19 90 19 50 15 90 15 60 19 80 9 60 16 80 11 20 16 10 80
endmodule
